# Fritzing sketch AutomatedChessboard (saved by Fritzing 0.9.9b)
breadboards: 4

parts:
  S1 = SWITCH-MOMENTARY-2 [package=reed_switch_pth]
  S2 = SWITCH-MOMENTARY-2 [package=reed_switch_pth]
  S3 = SWITCH-MOMENTARY-2 [package=reed_switch_pth]
  S4 = SWITCH-MOMENTARY-2 [package=reed_switch_pth]
  S5 = SWITCH-MOMENTARY-2 [package=reed_switch_pth]
  S6 = SWITCH-MOMENTARY-2 [package=reed_switch_pth]
  S7 = SWITCH-MOMENTARY-2 [package=reed_switch_pth]
  S8 = SWITCH-MOMENTARY-2 [package=reed_switch_pth]
  S9 = SWITCH-MOMENTARY-2 [package=reed_switch_pth]
  S10 = SWITCH-MOMENTARY-2 [package=reed_switch_pth]
  S11 = SWITCH-MOMENTARY-2 [package=reed_switch_pth]
  S12 = SWITCH-MOMENTARY-2 [package=reed_switch_pth]
  S13 = SWITCH-MOMENTARY-2 [package=reed_switch_pth]
  S14 = SWITCH-MOMENTARY-2 [package=reed_switch_pth]
  S15 = SWITCH-MOMENTARY-2 [package=reed_switch_pth]
  S16 = SWITCH-MOMENTARY-2 [package=reed_switch_pth]
  S17 = SWITCH-MOMENTARY-2 [package=reed_switch_pth]
  S18 = SWITCH-MOMENTARY-2 [package=reed_switch_pth]
  S19 = SWITCH-MOMENTARY-2 [package=reed_switch_pth]
  S20 = SWITCH-MOMENTARY-2 [package=reed_switch_pth]
  S21 = SWITCH-MOMENTARY-2 [package=reed_switch_pth]
  S22 = SWITCH-MOMENTARY-2 [package=reed_switch_pth]
  S23 = SWITCH-MOMENTARY-2 [package=reed_switch_pth]
  S24 = SWITCH-MOMENTARY-2 [package=reed_switch_pth]
  S25 = SWITCH-MOMENTARY-2 [package=reed_switch_pth]
  S26 = SWITCH-MOMENTARY-2 [package=reed_switch_pth]
  S27 = SWITCH-MOMENTARY-2 [package=reed_switch_pth]
  S28 = SWITCH-MOMENTARY-2 [package=reed_switch_pth]
  S29 = SWITCH-MOMENTARY-2 [package=reed_switch_pth]
  S30 = SWITCH-MOMENTARY-2 [package=reed_switch_pth]
  S31 = SWITCH-MOMENTARY-2 [package=reed_switch_pth]
  S32 = SWITCH-MOMENTARY-2 [package=reed_switch_pth]
  S33 = SWITCH-MOMENTARY-2 [package=reed_switch_pth]
  S34 = SWITCH-MOMENTARY-2 [package=reed_switch_pth]
  S35 = SWITCH-MOMENTARY-2 [package=reed_switch_pth]
  S36 = SWITCH-MOMENTARY-2 [package=reed_switch_pth]
  S37 = SWITCH-MOMENTARY-2 [package=reed_switch_pth]
  S38 = SWITCH-MOMENTARY-2 [package=reed_switch_pth]
  S39 = SWITCH-MOMENTARY-2 [package=reed_switch_pth]
  S40 = SWITCH-MOMENTARY-2 [package=reed_switch_pth]
  S41 = SWITCH-MOMENTARY-2 [package=reed_switch_pth]
  S42 = SWITCH-MOMENTARY-2 [package=reed_switch_pth]
  S43 = SWITCH-MOMENTARY-2 [package=reed_switch_pth]
  S44 = SWITCH-MOMENTARY-2 [package=reed_switch_pth]
  S45 = SWITCH-MOMENTARY-2 [package=reed_switch_pth]
  S46 = SWITCH-MOMENTARY-2 [package=reed_switch_pth]
  S47 = SWITCH-MOMENTARY-2 [package=reed_switch_pth]
  S48 = SWITCH-MOMENTARY-2 [package=reed_switch_pth]
  S49 = SWITCH-MOMENTARY-2 [package=reed_switch_pth]
  S50 = SWITCH-MOMENTARY-2 [package=reed_switch_pth]
  S51 = SWITCH-MOMENTARY-2 [package=reed_switch_pth]
  S52 = SWITCH-MOMENTARY-2 [package=reed_switch_pth]
  S53 = SWITCH-MOMENTARY-2 [package=reed_switch_pth]
  S54 = SWITCH-MOMENTARY-2 [package=reed_switch_pth]
  S55 = SWITCH-MOMENTARY-2 [package=reed_switch_pth]
  S56 = SWITCH-MOMENTARY-2 [package=reed_switch_pth]
  S57 = SWITCH-MOMENTARY-2 [package=reed_switch_pth]
  S58 = SWITCH-MOMENTARY-2 [package=reed_switch_pth]
  S59 = SWITCH-MOMENTARY-2 [package=reed_switch_pth]
  S60 = SWITCH-MOMENTARY-2 [package=reed_switch_pth]
  S61 = SWITCH-MOMENTARY-2 [package=reed_switch_pth]
  S62 = SWITCH-MOMENTARY-2 [package=reed_switch_pth]
  S63 = SWITCH-MOMENTARY-2 [package=reed_switch_pth]
  S64 = SWITCH-MOMENTARY-2 [package=reed_switch_pth]
  S66 = SWITCH-MOMENTARY-2 [package=reed_switch_pth]
  S67 = SWITCH-MOMENTARY-2 [package=reed_switch_pth]
  S71 = SWITCH-MOMENTARY-2 [package=reed_switch_pth]
  S72 = SWITCH-MOMENTARY-2 [package=reed_switch_pth]
  S74 = SWITCH-MOMENTARY-2 [package=reed_switch_pth]
  S78 = SWITCH-MOMENTARY-2 [package=reed_switch_pth]
  S79 = SWITCH-MOMENTARY-2 [package=reed_switch_pth]
  S80 = SWITCH-MOMENTARY-2 [package=reed_switch_pth]
  Part1 = Arduino Mega 2560 (Rev3)
  M1 = Stepper Motor - Bipolar
  M2 = Stepper Motor - Bipolar
  DRV_1 = DRV 8825 Stepper Motor Carrier, High Current [part_number="DRV 8825"]
  DRV_2 = DRV 8825 Stepper Motor Carrier, High Current [part_number="DRV 8825"]
  Part2 = IFR520 MOS module [package=THT]
  M3 = Grove Electromagnet
  Raspberry_Pi_1 = Raspberry Pi 4 [part_number=RPI-4-b]
  JACK1 = 2.1mm Barrel Jack with Terminal Block
  R1 = Resistor [tolerance=±5% resistance=10k package="2010 [SMD]"]
  R2 = Resistor [tolerance=±5% resistance=10k package="2010 [SMD]"]
  R3 = Resistor [tolerance=±5% resistance=10k package="2010 [SMD]"]
  R4 = Resistor [tolerance=±5% resistance=10k package="2010 [SMD]"]
  R5 = Resistor [tolerance=±5% resistance=10k package="2010 [SMD]"]
  R7 = Resistor [tolerance=±5% resistance=10k package="2010 [SMD]"]
  R8 = Resistor [tolerance=±5% resistance=10k package="2010 [SMD]"]
  R9 = Resistor [tolerance=±5% resistance=10k package="2010 [SMD]"]
  R10 = Resistor [tolerance=±5% resistance=10k package="2010 [SMD]"]
  R11 = Resistor [tolerance=±5% resistance=10k package="2010 [SMD]"]
  R12 = Resistor [tolerance=±5% resistance=10k package="2010 [SMD]"]
  R13 = Resistor [tolerance=±5% resistance=10k package="2010 [SMD]"]
  R14 = Resistor [tolerance=±5% resistance=10k package="2010 [SMD]"]
  R15 = Resistor [tolerance=±5% resistance=10k package="2010 [SMD]"]
  R16 = Resistor [tolerance=±5% resistance=10k package="2010 [SMD]"]
  R17 = Resistor [tolerance=±5% resistance=10k package="2010 [SMD]"]
  R18 = Resistor [tolerance=±5% resistance=10k package="2010 [SMD]"]
  R19 = Resistor [tolerance=±5% resistance=10k package="2010 [SMD]"]
  R20 = Resistor [tolerance=±5% resistance=10k package="2010 [SMD]"]
  R21 = Resistor [tolerance=±5% resistance=10k package="2010 [SMD]"]
  R22 = Resistor [tolerance=±5% resistance=10k package="2010 [SMD]"]
  R23 = Resistor [tolerance=±5% resistance=10k package="2010 [SMD]"]
  R24 = Resistor [tolerance=±5% resistance=10k package="2010 [SMD]"]
  R26 = Resistor [tolerance=±5% resistance=10k package="2010 [SMD]"]
  R28 = Resistor [tolerance=±5% resistance=10k package="2010 [SMD]"]
  R29 = Resistor [tolerance=±5% resistance=10k package="2010 [SMD]"]
  R30 = Resistor [tolerance=±5% resistance=10k package="2010 [SMD]"]
  R31 = Resistor [tolerance=±5% resistance=10k package="2010 [SMD]"]
  R32 = Resistor [tolerance=±5% resistance=10k package="2010 [SMD]"]
  R33 = Resistor [tolerance=±5% resistance=10k package="2010 [SMD]"]
  R34 = Resistor [tolerance=±5% resistance=10k package="2010 [SMD]"]
  R35 = Resistor [tolerance=±5% resistance=10k package="2010 [SMD]"]
  R36 = Resistor [tolerance=±5% resistance=10k package="2010 [SMD]"]
  R37 = Resistor [tolerance=±5% resistance=10k package="2010 [SMD]"]
  R38 = Resistor [tolerance=±5% resistance=10k package="2010 [SMD]"]
  R39 = Resistor [tolerance=±5% resistance=10k package="2010 [SMD]"]
  R40 = Resistor [tolerance=±5% resistance=10k package="2010 [SMD]"]
  R41 = Resistor [tolerance=±5% resistance=10k package="2010 [SMD]"]
  R42 = Resistor [tolerance=±5% resistance=10k package="2010 [SMD]"]
  R43 = Resistor [tolerance=±5% resistance=10k package="2010 [SMD]"]
  R44 = Resistor [tolerance=±5% resistance=10k package="2010 [SMD]"]
  R45 = Resistor [tolerance=±5% resistance=10k package="2010 [SMD]"]
  R46 = Resistor [tolerance=±5% resistance=10k package="2010 [SMD]"]
  R47 = Resistor [tolerance=±5% resistance=10k package="2010 [SMD]"]
  R48 = Resistor [tolerance=±5% resistance=10k package="2010 [SMD]"]
  R49 = Resistor [tolerance=±5% resistance=10k package="2010 [SMD]"]
  R50 = Resistor [tolerance=±5% resistance=10k package="2010 [SMD]"]
  R51 = Resistor [tolerance=±5% resistance=10k package="2010 [SMD]"]
  R52 = Resistor [tolerance=±5% resistance=10k package="2010 [SMD]"]
  R53 = Resistor [tolerance=±5% resistance=10k package="2010 [SMD]"]
  R54 = Resistor [tolerance=±5% resistance=10k package="2010 [SMD]"]
  R56 = Resistor [tolerance=±5% resistance=10k package="2010 [SMD]"]
  R57 = Resistor [tolerance=±5% resistance=10k package="2010 [SMD]"]
  R58 = Resistor [tolerance=±5% resistance=10k package="2010 [SMD]"]
  R59 = Resistor [tolerance=±5% resistance=10k package="2010 [SMD]"]
  R60 = Resistor [tolerance=±5% resistance=10k package="2010 [SMD]"]
  R61 = Resistor [tolerance=±5% resistance=10k package="2010 [SMD]"]
  R62 = Resistor [tolerance=±5% resistance=10k package="2010 [SMD]"]
  R63 = Resistor [tolerance=±5% resistance=10k package="2010 [SMD]"]
  R64 = Resistor [tolerance=±5% resistance=10k package="2010 [SMD]"]
  R65 = Resistor [tolerance=±5% resistance=10k package="2010 [SMD]"]
  R66 = Resistor [tolerance=±5% resistance=10k package="2010 [SMD]"]
  R67 = Resistor [tolerance=±5% resistance=10k package="2010 [SMD]"]
  R68 = Resistor [tolerance=±5% resistance=10k package="2010 [SMD]"]
  R69 = Resistor [tolerance=±5% resistance=10k package="2010 [SMD]"]
  R70 = Resistor [tolerance=±5% resistance=10k package="2010 [SMD]"]
  R71 = Resistor [tolerance=±5% resistance=10k package="2010 [SMD]"]
  R72 = Resistor [tolerance=±5% resistance=10k package="2010 [SMD]"]
  R74 = Resistor [tolerance=±5% resistance=10k package="2010 [SMD]"]
  R75 = Resistor [tolerance=±5% resistance=10k package="2010 [SMD]"]
  R76 = Resistor [tolerance=±5% resistance=10k package="2010 [SMD]"]
  R77 = Resistor [tolerance=±5% resistance=10k package="2010 [SMD]"]
  Part3 = Analog Digital MUX Breakout
  M4 = bb-usb-cable [package=THT]  # not connected
  C1 = Capacitor Polarized [package=cpol-radial-100uf-25v]
  C2 = Capacitor Polarized [package=cpol-radial-100uf-25v]
  R78 = Resistor [tolerance=±5% resistance=10k package="2512 [SMD]"]
  U1 = LCD-16X2 [package=lcd-16x2_nosilk]
  S81 = Round Pushbutton
  LCM1602_IIC1 = LCM1602 IIC [part_number="LCM1602 IIC" chip_label="LCM1602 IIC" package="DIP (Dual Inline) [THT]"]
  M5 = bb-usb-cable [package=THT]  # not connected

nets:
  5V: S1.1, S2.1, S3.1, S4.1, S5.1, S6.1, S7.1, S8.1, S9.1, S10.1, S11.1, S12.1, S13.1, S14.1, S15.1, S16.1, S17.1, S18.1, S19.1, S20.1, S21.1, S22.1, S23.1, S24.1, S25.1, S26.1, S27.1, S28.1, S29.1, S30.1, S31.1, S32.1, S33.1, S34.1, S35.1, S36.1, S37.1, S38.1, S39.1, S40.1, S41.1, S42.1, S43.1, S44.1, S45.1, S46.1, S47.1, S48.1, S49.1, S50.1, S51.1, S52.1, S53.1, S54.1, S55.1, S56.1, S57.1, S58.1, S59.1, S60.1, S61.1, S62.1, S63.1, S64.1, S66.1, S67.1, S71.1, S72.1, S74.1, S78.1, S79.1, S80.1, Part1.5V, Part3.VCC
  N1: S1.2, R26.Pin_0
  N2: S2.2, R5.Pin_0
  N3: S3.2, R8.Pin_0
  N4: S4.2, R32.Pin_0
  N5: S5.2, R14.Pin_0
  N6: S6.2, R38.Pin_0
  N7: S7.2, R10.Pin_0
  N8: S8.2, R36.Pin_0
  N9: S9.2, R49.Pin_0
  N10: S10.2, R61.Pin_0
  N11: S11.2, R71.Pin_0
  N12: S12.2, R54.Pin_0
  N13: S13.2, R66.Pin_0
  N14: S14.2, R44.Pin_0
  N15: S15.2, R77.Pin_0
  N16: S16.2, R68.Pin_0
  N17: S17.2, R47.Pin_0
  N18: S18.2, R34.Pin_0
  N19: S19.2, R21.Pin_0
  N20: S20.2, R59.Pin_0
  N21: S21.2, R72.Pin_0
  N22: S22.2, R75.Pin_0
  N23: S23.2, R11.Pin_0
  N24: S24.2, R4.Pin_0
  N25: S25.2, R52.Pin_0
  N26: S26.2, R24.Pin_0
  N27: S27.2, R57.Pin_0
  N28: S28.2, R64.Pin_0
  N29: S29.2, R69.Pin_0
  N30: S30.2, R41.Pin_0
  N31: S31.2, R30.Pin_0
  N32: S32.2, R17.Pin_0
  N33: S33.2, R45.Pin_0
  N34: S34.2, R37.Pin_0
  N35: S35.2, R19.Pin_0
  N36: S36.2, R62.Pin_0
  N37: S37.2, R51.Pin_0
  N38: S38.2, R48.Pin_0
  N39: S39.2, R9.Pin_0
  N40: S40.2, R31.Pin_0
  N41: S41.2, R50.Pin_0
  N42: S42.2, R2.Pin_0
  N43: S43.2, R60.Pin_0
  N44: S44.2, R67.Pin_0
  N45: S45.2, R70.Pin_0
  N46: S46.2, R39.Pin_0
  N47: S47.2, R28.Pin_0
  N48: S48.2, R15.Pin_0
  N49: S49.2, R43.Pin_0
  N50: S50.2, R33.Pin_0
  N51: S51.2, R12.Pin_0
  N52: S52.2, R58.Pin_0
  N53: S53.2, R76.Pin_0
  N54: S54.2, R63.Pin_0
  N55: S55.2, R7.Pin_0
  N56: S56.2, R3.Pin_0
  N57: S57.2, R53.Pin_0
  N58: S58.2, R23.Pin_0
  N59: S59.2, R46.Pin_0
  N60: S60.2, R65.Pin_0
  N61: S61.2, R74.Pin_0
  N62: S62.2, R13.Pin_0
  N63: S63.2, R29.Pin_0
  N64: S64.2, R16.Pin_0
  N65: S66.2, R56.Pin_0
  N66: S67.2, R42.Pin_0
  N67: S71.2, R22.Pin_0
  N68: S72.2, R18.Pin_0
  N69: S74.2, R1.Pin_0
  N70: S78.2, R40.Pin_0
  N71: S79.2, R20.Pin_0
  N72: S80.2, R35.Pin_0
  GND: Part1.A8, Part1.A9, Part1.A10, Part1.A11, Part1.A12, Part1.A13, Part1.A14, Part1.A15, Part1.A4, Part1.A5, Part1.A6, Part1.A7, Part1.D21/SCL, Part1.D20/SDA, Part1.D19/RX1, Part1.D18/TX1, Part1.D17_PWM/RX2, Part1.D16_PWM/TX2, Part1.D15/RX3, Part1.D14/TX3, Part1.D13_PWM, Part1.D12_PWM, Part1.D11_PWM, Part1.D10_PWM, Part1.D9_PWM, Part1.D8_PWM, Part1.GND, Part1.D0_RX0, Part1.D1_TX0, Part1.D2_PWM, Part1.D3_PWM, Part1.D4_PWM, Part1.D5_PWM, Part1.D6_PWM, Part1.D7_PWM, Part1.D22, Part1.D23, Part1.D24, Part1.D25, Part1.D26, Part1.D27, Part1.D28, Part1.D29, Part1.D30, Part1.D31, Part1.D32, Part1.D33, Part1.D34, Part1.D35, Part1.D36, Part1.D37, Part1.D38, Part1.D39, Part1.D40, Part1.D41, Part1.D42, Part1.D43, Part1.D44, Part1.D45, Part1.D46, Part1.D47, Part1.D48, Part1.D49, Part1.D51, Part1.D53, R1.Pin_1, R2.Pin_1, R3.Pin_1, R4.Pin_1, R5.Pin_1, R7.Pin_1, R8.Pin_1, R9.Pin_1, R10.Pin_1, R11.Pin_1, R12.Pin_1, R13.Pin_1, R14.Pin_1, R15.Pin_1, R16.Pin_1, R17.Pin_1, R18.Pin_1, R19.Pin_1, R20.Pin_1, R21.Pin_1, R22.Pin_1, R23.Pin_1, R24.Pin_1, R26.Pin_1, R28.Pin_1, R29.Pin_1, R30.Pin_1, R31.Pin_1, R32.Pin_1, R33.Pin_1, R34.Pin_1, R35.Pin_1, R36.Pin_1, R37.Pin_1, R38.Pin_1, R39.Pin_1, R40.Pin_1, R41.Pin_1, R42.Pin_1, R43.Pin_1, R44.Pin_1, R45.Pin_1, R46.Pin_1, R47.Pin_1, R48.Pin_1, R49.Pin_1, R50.Pin_1, R51.Pin_1, R52.Pin_1, R53.Pin_1, R54.Pin_1, R56.Pin_1, R57.Pin_1, R58.Pin_1, R59.Pin_1, R60.Pin_1, R61.Pin_1, R62.Pin_1, R63.Pin_1, R64.Pin_1, R65.Pin_1, R66.Pin_1, R67.Pin_1, R68.Pin_1, R69.Pin_1, R70.Pin_1, R71.Pin_1, R72.Pin_1, R74.Pin_1, R75.Pin_1, R76.Pin_1, R77.Pin_1, Part3.C0, Part3.C1, Part3.C2, Part3.C3, Part3.C4, Part3.C5, Part3.C6, Part3.C7, Part3.GND
  N73: Part1.A0, Part3.S0
  N74: Part1.A1, Part3.S1
  N75: Part1.A2, Part3.S2
  N76: Part1.A3, Part3.S3
  N77: M1.C, DRV_2.OUT_2A
  N78: M1.B, DRV_2.OUT_1A
  N79: M1.D, DRV_2.OUT_1B
  N80: M2.A, DRV_1.OUT_2B
  N81: M2.C, DRV_1.OUT_2A
  N82: M2.B, DRV_1.OUT_1A
  N83: M2.D, DRV_1.OUT_1B
  VCC: DRV_1.RESET, DRV_1.SLEEP, DRV_2.RESET, DRV_2.SLEEP, Part2.VCC, Raspberry_Pi_1.5V
  N84: DRV_1.STEP, Raspberry_Pi_1.GPIO26
  N85: DRV_1.DIRECTION, Raspberry_Pi_1.GPIO19
  VIN: DRV_1.VOLTAGE_ST/_MT, DRV_2.VOLTAGE_ST/_MT, Part2.VIN, JACK1.POS, C1.+, C2.+, LCM1602_IIC1.VCC
  GND_2: DRV_1.GROUND_ST/_MT, DRV_1.GROUND_LOG, DRV_2.DIRECTION, DRV_2.GROUND_ST/_MT, DRV_2.GROUND_LOG, Part2.GND, Raspberry_Pi_1.GND, Raspberry_Pi_1.GPIO5, Raspberry_Pi_1.GPIO6, Raspberry_Pi_1.GPIO12, JACK1.NEG, C1.-, C2.-, R78.Pin_1, LCM1602_IIC1.GND
  N86: DRV_2.STEP, Raspberry_Pi_1.GPIO13
  N87: Part2.SIG, Raspberry_Pi_1.GPIO20, Raspberry_Pi_1.GPIO16
  N88: Part2.V+, M3.VCC
  N89: Part2.V-, M3.GND
  N90: Raspberry_Pi_1.GPIO2, LCM1602_IIC1.SDA
  N91: Raspberry_Pi_1.GPIO3, Raspberry_Pi_1.GPIO4, LCM1602_IIC1.SCL
  N92: R78.Pin_0, S81.leg0
  VSS: U1.VSS, LCM1602_IIC1.VSS
  VDD: U1.VDD, LCM1602_IIC1.VDD
  N93: U1.VO, LCM1602_IIC1.V0
  N94: U1.RS, LCM1602_IIC1.RS
  N95: U1.R_W, LCM1602_IIC1.RW
  N96: U1.E, LCM1602_IIC1.E
  N97: U1.DB0, LCM1602_IIC1.D0
  N98: U1.DB1, LCM1602_IIC1.D1
  N99: U1.DB2, LCM1602_IIC1.D2
  N100: U1.DB3, LCM1602_IIC1.D3
  N101: U1.DB4, LCM1602_IIC1.D4
  N102: U1.DB5, LCM1602_IIC1.D5
  N103: U1.DB6, LCM1602_IIC1.D6
  N104: U1.DB7, LCM1602_IIC1.D7
  N105: U1.A, LCM1602_IIC1.A
  N106: U1.K, LCM1602_IIC1.K

custom parts:
  Grove Electromagnet: Grove Electromagnet.
  Raspberry Pi 4: The RPi4, a faster version of the awesome Raspberry Pi 2 B ARM Board with 40 pin gpio. Ready for special Raspberry Pi B+ and RPi2 Hat (Hardware attached (on) top)
  bb-usb-cable: Breadboard only, no connectors USB cable for the Raspberry PIs.
  LCM1602 IIC: I2C-Module to use a 1602 or 2004 LCD on with the wire.h libory Serial LCD Modul
